# Fritzing sketch yagarto on netduino (saved by Fritzing 0.7.10b)

parts:
  Netduino1 = Netduino
  Part1 = FTDI Basic Programmer
  Part2 = FTDI Basic Programmer
  LED1 = LED - 5mm [color="Orange (620nm)" package="5 mm [THT]"]
  LED3 = LED - 5mm [color="Orange (605nm)" package="5 mm [THT]"]
  LED4 = LED - 5mm [color="Red (633nm)" package="5 mm [THT]"]
  R1 = Rotary Potentiometer (Large) [maximum_resistance=10kΩ package=THT]
  S1 = Pushbutton [package="[THT]"]
  LED2 = LED - 5mm [color="Yellow (595nm)" package="5 mm [THT]"]
  R2 = Resistor [tolerance=±5% resistance=1k package=THT]
  R3 = Resistor [tolerance=±5% resistance=1k package=THT]
  R4 = Resistor [tolerance=±5% resistance=1k package=THT]
  R5 = Resistor [tolerance=±5% resistance=1k package=THT]
  R6 = Rotary Potentiometer (Large) [maximum_resistance=10kΩ package=THT]

nets:
  GND: Netduino1.GND#1, Part1.GND, Part2.GND, R2.Pin_0, R3.Pin_0, R4.Pin_0, R5.Pin_0
  N1: Netduino1.D7_RTS1, LED4.anode
  N2: Netduino1.D6_PWM1, LED1.anode
  N3: Netduino1.D5_PWM0, LED3.anode
  N4: Netduino1.D4_CS0, LED2.anode
  N5: Netduino1.D3_TX1, Part2.RXI
  N6: Netduino1.D2_RX1, Part2.TXO
  N7: Netduino1.D1_TX0, Part1.RXI
  N8: Netduino1.D0_RX0, Part1.TXO
  N9: Netduino1.3V3, R1.leg1, R6.leg1
  N10: Netduino1.GND#20, R1.leg2, R6.leg2
  N11: Netduino1.A0, R1.wiper
  N12: Netduino1.A3, R6.wiper
  N13: Part2.POWER, S1.Pin_3, S1.Pin_4

notes:
  Debug UART (DBGU)
  USART0
  Switch connected to ERASE pad
  Both FTDI Basic are of 3.3V
  LEDs
  Potentioneters connected to ADC
